# Fritzing sketch BurgerDisk (saved by Fritzing 1.0.1rc)
circuit board: 7.40538cm x 7.03119cm
breadboards: 1

parts:
  150Ω = Resistor [tolerance=±5% power=0.25 resistance=220 package=THT]
  -_LED_+ = LED - 3mm [color="Red (633nm)" current=0.030 package="3 mm [THT]"]
  Daisy_out_2 = female pin header, 9 pins [form="♀ (female)"]
  Daisy_out = female pin header, 10 pins [form="♀ (female)"]
  NANO = female pin header, 15 pins [form="♀ (female)"]
  NANO_2 = female pin header, 15 pins [form="♀ (female)"]
  microSD = MicroSD Card Module
  Pad1 = Pad [width=3 height=2 connect=center]
  Pad2 = Pad [width=3 height=2 connect=center]
  Pad3 = Pad [width=3 height=2 connect=center]
  Pad4 = Pad [width=3 height=2 connect=center]
  Pad5 = Pad [width=3 height=2 connect=center]
  Pad6 = Pad [width=3 height=2 connect=center]
  Pad7 = Pad [width=3 height=2 connect=center]
  Pad8 = Pad [width=3 height=2 connect=center]
  Pad9 = Pad [width=3 height=2 connect=center]
  Pad10 = Pad [width=3 height=2 connect=center]
  Pad22 = Pad [width=3 height=2 connect=center]
  Pad24 = Pad [width=3 height=2 connect=center]
  Pad28 = Pad [width=3 height=2 connect=center]
  Pad21 = Pad [width=3 height=2 connect=center]
  Pad26 = Pad [width=3 height=2 connect=center]
  Pad25 = Pad [width=3 height=2 connect=center]
  Pad20 = Pad [width=3 height=2 connect=center]
  Pad23 = Pad [width=3 height=2 connect=center]
  Pad27 = Pad [width=3 height=2 connect=center]
  Daisy_in = shrouded pin header, 20 pins [form="♂ (shrouded male)"]
  GND/TX = female pin header, 2 pins [form="♀ (female)"]
  IIgs = female pin header, 2 pins [form="♀ (female)"]
  J5 = female pin header, 6 pins [form="♀ (female)"]
  1N5818 = Diode [package=diode-1n4148]
  SPadv = female pin header, 2 pins [form="♀ (female)"]
  330Ω = Resistor [tolerance=±5% power=0.25 resistance=220 package=THT]
  1N4448 = Diode [package=diode-1n4148]
  1N4448_2 = Diode [package=diode-1n4148]

nets:
  N1: 150Ω.Pin_0, NANO_2.pin8
  N2: 150Ω.Pin_1, -_LED_+.anode
  N3: -_LED_+.cathode, Daisy_out.pin1, Daisy_out.pin2, Daisy_out.pin3, NANO.pin4, microSD.GND, Pad1.pad, Pad2.pad, Pad3.pad, Daisy_in.pin1, Daisy_in.pin2, Daisy_in.pin3, GND/TX.pin2, J5.pin1, 330Ω.Pin_1
  N4: Daisy_out_2.pin1, NANO.pin5, Pad24.pad, Daisy_in.pin20
  N5: Daisy_out_2.pin2, NANO.pin6, Pad22.pad, Daisy_in.pin19
  N6: Daisy_out_2.pin3, NANO.pin7, Pad28.pad, Daisy_in.pin18
  N7: Daisy_out_2.pin4, NANO.pin11, Pad21.pad
  N8: Daisy_out_2.pin5, Pad26.pad, Daisy_in.pin16
  N9: Daisy_out_2.pin6, NANO_2.pin11, Pad25.pad
  N10: Daisy_out_2.pin7, NANO_2.pin10, Pad20.pad
  N11: Daisy_out_2.pin8, Pad23.pad, Daisy_in.pin13, 1N4448.A
  N12: Daisy_out_2.pin9, NANO.pin10, Pad27.pad, Daisy_in.pin12
  N13: Daisy_out.pin4, Pad4.pad, Daisy_in.pin4
  N14: Daisy_out.pin5, Pad5.pad, Daisy_in.pin5
  N15: Daisy_out.pin6, Pad6.pad, Daisy_in.pin6, 1N5818.A
  N16: Daisy_out.pin7, Daisy_out.pin8, Pad7.pad, Pad8.pad, Daisy_in.pin7, Daisy_in.pin8
  N17: Daisy_out.pin9, NANO_2.pin9, Pad9.pad
  N18: Daisy_out.pin10, Pad10.pad, Daisy_in.pin11, 1N4448_2.A
  N19: NANO.pin1, GND/TX.pin1
  N20: NANO.pin8, Daisy_in.pin17
  N21: NANO.pin9, 1N4448.C
  N22: NANO.pin12, IIgs.pin2
  N23: NANO.pin13, microSD.CS, J5.pin6
  N24: NANO.pin14, microSD.MOSI, J5.pin4
  N25: NANO.pin15, microSD.MISO, J5.pin3
  N26: NANO_2.pin4, microSD.VCC, J5.pin2, 1N5818.C
  N27: NANO_2.pin7, 1N4448_2.C
  N28: NANO_2.pin12, Daisy_in.pin14
  N29: NANO_2.pin15, microSD.SCK, J5.pin5
  N30: Daisy_in.pin9, IIgs.pin1
  N31: Daisy_in.pin15, SPadv.pin2
  N32: SPadv.pin1, 330Ω.Pin_0

notes:
  GND
  +5V
  A5
  A4
  A3
  A2
  A1
  A0
  D12
  D11
  D10
  D7
  D6
  D5
  D4
  D3
  D2
  D8
  D9
  USB
  NANO
  EN35
  -12V
  +12V
  DRV2
  WPROT
  PH0
  PH1
  PH2
  PH3
  WREQ
  HDSEL
  DR1
  RD
  WR
  UART
  DR2
  +12
  +5
  -12
  WPRT
  SEL
  WRQ
  MISO
  MOSI
  SCK
  CS
  FOR APPLE II ONLY
  BURGERDISK
  jumpers when connecting to a
  5.25" controller!
  Never close IIgs or SPadv
  CC BY-SA - colino.net
  conn
  TX
  D13
