# Fritzing sketch BurgerDisk (saved by Fritzing 1.0.1rc)
circuit board: 7.40538cm x 7.03119cm
breadboards: 1

parts:
  150Ω = Resistor [tolerance=±5% power=0.25 resistance=150 package=THT]
  -_LED_+ = LED - 3mm [color="Red (633nm)" current=0.030 package="3 mm [THT]"]
  NANO = female pin header, 15 pins [form="♀ (female)"]
  NANO_2 = female pin header, 15 pins [form="♀ (female)"]
  Pad1 = Pad [width=4 height=2 connect=center]
  Pad2 = Pad [width=4 height=2 connect=center]
  Pad3 = Pad [width=4 height=2 connect=center]
  Pad4 = Pad [width=4 height=2 connect=center]
  Pad5 = Pad [width=4 height=2 connect=center]
  Pad6 = Pad [width=4 height=2 connect=center]
  Pad7 = Pad [width=4 height=2 connect=center]
  Pad8 = Pad [width=4 height=2 connect=center]
  Pad9 = Pad [width=4 height=2 connect=center]
  Pad10 = Pad [width=4 height=2 connect=center]
  Pad22 = Pad [width=4 height=2 connect=center]
  Pad24 = Pad [width=4 height=2 connect=center]
  Pad28 = Pad [width=4 height=2 connect=center]
  Pad21 = Pad [width=4 height=2 connect=center]
  Pad26 = Pad [width=4 height=2 connect=center]
  Pad25 = Pad [width=4 height=2 connect=center]
  Pad20 = Pad [width=4 height=2 connect=center]
  Pad23 = Pad [width=4 height=2 connect=center]
  Pad27 = Pad [width=4 height=2 connect=center]
  Daisy_in = shrouded pin header, 20 pins [form="♂ (shrouded male)"]
  GND/TX = female pin header, 2 pins [form="♀ (female)"]
  J5 = female pin header, 6 pins [form="♀ (female)"]
  330Ω = Resistor [tolerance=±5% power=0.25 resistance=330 package=THT]
  RD_1N4448 = Diode [part_number=1N4448 package=diode-1n4148]
  WPRT_1N4448 = Diode [part_number=1N4448 package=diode-1n4148]
  GND = female pin header, 1 pin [form="♀ (female)"]
  GND_2 = female pin header, 1 pin [form="♀ (female)"]
  E35 = female pin header, 1 pin [form="♀ (female)"]
  -12 = female pin header, 1 pin [form="♀ (female)"]
  +5 = female pin header, 1 pin [form="♀ (female)"]
  +12 = female pin header, 1 pin [form="♀ (female)"]
  +12_2 = female pin header, 1 pin [form="♀ (female)"]
  DR2 = female pin header, 1 pin [form="♀ (female)"]
  WPT = female pin header, 1 pin [form="♀ (female)"]
  P1 = female pin header, 1 pin [form="♀ (female)"]
  P2 = female pin header, 1 pin [form="♀ (female)"]
  P3 = female pin header, 1 pin [form="♀ (female)"]
  WRQ = female pin header, 1 pin [form="♀ (female)"]
  HSL = female pin header, 1 pin [form="♀ (female)"]
  DR1 = female pin header, 1 pin [form="♀ (female)"]
  RD = female pin header, 1 pin [form="♀ (female)"]
  WR = female pin header, 1 pin [form="♀ (female)"]
  GND_3 = female pin header, 1 pin [form="♀ (female)"]
  P0 = female pin header, 1 pin [form="♀ (female)"]
  microSD_-_under_main_PCB = MicroSD Card Module
  U1 = Sharp PC817 [package=THT]
  470Ω = Resistor [tolerance=±5% power=0.25 resistance=470 package=THT]
  10kΩ = Resistor [tolerance=±5% power=0.25 resistance=10k package=THT]
  1N5818 = Schottky Diode [part_number=1N5818 package="300 mil [THT]"]
  1kΩ = Resistor [tolerance=±5% power=0.25 resistance=220 package=THT]

nets:
  N1: 150Ω.Pin_0, NANO_2.pin8
  N2: 150Ω.Pin_1, -_LED_+.anode
  N3: -_LED_+.cathode, NANO.pin4, Pad1.pad, Pad2.pad, Pad3.pad, Daisy_in.pin1, Daisy_in.pin2, Daisy_in.pin3, GND/TX.pin2, J5.pin1, 330Ω.Pin_1, GND.pin1, GND_2.pin1, GND_3.pin1, microSD_-_under_main_PCB.GND, U1.Pin_2, 10kΩ.Pin_0
  N4: NANO.pin1, GND/TX.pin1
  N5: NANO.pin5, Pad24.pad, Daisy_in.pin20, P0.pin1
  N6: NANO.pin6, Pad22.pad, Daisy_in.pin19, P1.pin1
  N7: NANO.pin7, Pad28.pad, Daisy_in.pin18, P2.pin1
  N8: NANO.pin8, Daisy_in.pin17
  N9: NANO.pin9, RD_1N4448.C
  N10: NANO.pin10, Pad27.pad, Daisy_in.pin12, WR.pin1
  N11: NANO.pin11, Pad21.pad, P3.pin1
  N12: NANO.pin12, 1kΩ.Pin_1
  N13: NANO.pin13, J5.pin6, microSD_-_under_main_PCB.CS
  N14: NANO.pin14, J5.pin4, microSD_-_under_main_PCB.MOSI
  N15: NANO.pin15, J5.pin3, microSD_-_under_main_PCB.MISO
  N16: NANO_2.pin4, J5.pin2, microSD_-_under_main_PCB.VCC, U1.Pin_4, 1N5818.cathode
  N17: NANO_2.pin7, WPRT_1N4448.C
  N18: NANO_2.pin9, Pad9.pad, DR2.pin1
  N19: NANO_2.pin10, Pad20.pad, DR1.pin1
  N20: NANO_2.pin11, Pad25.pad, HSL.pin1
  N21: NANO_2.pin12, Daisy_in.pin14
  N22: NANO_2.pin15, J5.pin5, microSD_-_under_main_PCB.SCK
  N23: Pad4.pad, Daisy_in.pin4, E35.pin1
  N24: Pad5.pad, Daisy_in.pin5, -12.pin1
  N25: Pad6.pad, Daisy_in.pin6, +5.pin1, 1N5818.anode
  N26: Pad7.pad, Pad8.pad, Daisy_in.pin7, Daisy_in.pin8, +12.pin1, +12_2.pin1
  N27: Pad10.pad, Daisy_in.pin11, WPRT_1N4448.A, WPT.pin1
  N28: Pad26.pad, Daisy_in.pin16, WRQ.pin1
  N29: Pad23.pad, Daisy_in.pin13, RD_1N4448.A, RD.pin1
  N30: Daisy_in.pin9, 470Ω.Pin_1
  N31: Daisy_in.pin15, 330Ω.Pin_0
  N32: U1.Pin_1, 470Ω.Pin_0
  N33: U1.Pin_3, 10kΩ.Pin_1, 1kΩ.Pin_0

notes:
  GD
  +5V
  A5
  A4
  A3
  A2
  A1
  A0
  D12
  D11
  D10
  D7
  D6
  D5
  D4
  D3
  D2
  D8
  D9
  USB
  NANO
  UART
  DR2
  +12
  +5
  -12
  E35
  GND
  WPRT
  WR
  RD
  DR1
  HSL
  WRQ
  PH3
  PH2
  PH1
  PH0
  MISO
  MOSI
  SCK
  CS
  For Apple II only
  BurgerDisk
  CC BY-SA - colino.net
  conn
  TX
  D13
  Daisy out
  Daisy in
