# Fritzing sketch db19-idc20-adapter (saved by Fritzing 1.0.1rc)
circuit board: 1.80915cm x 3.33989cm
breadboards: 1

parts:
  Daisy_in1 = shrouded pin header, 20 pins [form="♂ (shrouded male)"]
  Pad29 = Pad [width=4 height=2 connect=center]
  Pad30 = Pad [width=4 height=2 connect=center]
  Pad31 = Pad [width=4 height=2 connect=center]
  Pad32 = Pad [width=4 height=2 connect=center]
  Pad33 = Pad [width=4 height=2 connect=center]
  Pad34 = Pad [width=4 height=2 connect=center]
  Pad35 = Pad [width=4 height=2 connect=center]
  Pad36 = Pad [width=4 height=2 connect=center]
  Pad37 = Pad [width=4 height=2 connect=center]
  Pad38 = Pad [width=4 height=2 connect=center]
  Pad39 = Pad [width=4 height=2 connect=center]
  Pad40 = Pad [width=4 height=2 connect=center]
  Pad41 = Pad [width=4 height=2 connect=center]
  Pad42 = Pad [width=4 height=2 connect=center]
  Pad43 = Pad [width=4 height=2 connect=center]
  Pad44 = Pad [width=4 height=2 connect=center]
  Pad45 = Pad [width=4 height=2 connect=center]
  Pad46 = Pad [width=4 height=2 connect=center]
  Pad47 = Pad [width=4 height=2 connect=center]

nets:
  N1: Daisy_in1.pin1, Pad47.pad
  N2: Daisy_in1.pin2, Pad46.pad
  N3: Daisy_in1.pin3, Pad45.pad
  N4: Daisy_in1.pin4, Pad44.pad
  N5: Daisy_in1.pin5, Pad43.pad
  N6: Daisy_in1.pin6, Pad42.pad
  N7: Daisy_in1.pin7, Pad41.pad
  N8: Daisy_in1.pin8, Pad40.pad
  N9: Daisy_in1.pin9, Pad39.pad
  N10: Daisy_in1.pin11, Pad38.pad
  N11: Daisy_in1.pin12, Pad37.pad
  N12: Daisy_in1.pin13, Pad36.pad
  N13: Daisy_in1.pin14, Pad35.pad
  N14: Daisy_in1.pin15, Pad34.pad
  N15: Daisy_in1.pin16, Pad33.pad
  N16: Daisy_in1.pin17, Pad32.pad
  N17: Daisy_in1.pin18, Pad31.pad
  N18: Daisy_in1.pin19, Pad29.pad
  N19: Daisy_in1.pin20, Pad30.pad

notes:
  WPROT
  +12V
  +5V
  -12V
  EN35
  GND
  DRV2
  PH0
  PH1
  PH2
  PH3
  WREQ
  HDSEL
  DRV1
  RD
  WR
  WRQ
  SEL
  DR1
  WPRT
  -12
  +5
  +12
  DR2
